# Fritzing sketch arduino_ir_receiver (saved by Fritzing 0.8.3b)
breadboards: 1

parts:
  Part1 = Arduino Micro (Rev3)  # not connected
  IR1 = TSOP312.., 314.. [part_number=TSOP382 package=THT]
  C1 = Electrolytic Capacitor [capacitance=1μF package="0405 [SMD, electrolytic]"]
  LED1 = LED - 5mm [color="Red (633nm)" package="5 mm [THT]"]
  LED2 = LED - 5mm [color="Green (555nm)" package="5 mm [THT]"]
  R1 = Resistor [tolerance=±5% resistance=47 package=THT]
  IC1 = IC, DIP package, 8 pins [chip_label=MCP4131 part_number="Microchip MCP4131"]
  R2 = PHOTOCELL [package=photocell]
  R3 = Resistor [tolerance=±5% resistance=10k package=THT]
  R4 = Resistor [tolerance=±5% resistance=220 package=THT]
  R5 = Resistor [tolerance=±5% resistance=220 package=THT]
  IC3 = IC, DIP package, 8 pins [chip_label=MCP4131 part_number="Microchip MCP4131"]

nets:
  N1: IR1.GND, C1.+, R1.Pin_0
  N2: IR1.Vs, C1.-, IC1.pin4, IC1.pin7, R3.Pin_0, R4.Pin_0, R5.Pin_0, IC3.pin4, IC3.pin7
  N3: LED1.cathode, R5.Pin_1
  N4: LED1.anode, IC3.pin6
  N5: LED2.cathode, R4.Pin_1
  N6: LED2.anode, IC1.pin6
  N7: R1.Pin_1, IC1.pin5, IC1.pin8, R2.P$2, IC3.pin8
  N8: IC1.pin2, IC3.pin2
  N9: IC1.pin3, IC3.pin3
  N10: R2.P$1, R3.Pin_1
